// Logisim project sleepyu.circ as structural Verilog: 7 circuits, main circuit main
module main (
);

  wire execution_1_memread_ex, execution_1_memtoreg_ex, execution_1_memwrite_ex, execution_1_writeenable_ex,
       instruction_decoding_1_aluop_id, instruction_decoding_1_memread_id,
       instruction_decoding_1_memtoreg_id, instruction_decoding_1_memwrite_id,
       instruction_decoding_1_writeenable_id, memory_access_1_memtoreg_me, memory_access_1_writeenable_me,
       PC_Clock_out;
  wire [1:0] execution_1_writereg_ex, instruction_decoding_1_rd_id, instruction_decoding_1_rs_id,
       instruction_decoding_1_rt_id, memory_access_1_writereg_me;
  wire [3:0] binary_to_bcd_converter_1_p2, binary_to_bcd_converter_1_p3, binary_to_bcd_converter_2_p2,
       binary_to_bcd_converter_2_p3, binary_to_bcd_converter_2_p4, binary_to_bcd_converter_3_p2,
       binary_to_bcd_converter_3_p3, binary_to_bcd_converter_3_p4, binary_to_bcd_converter_4_p2,
       binary_to_bcd_converter_4_p3, binary_to_bcd_converter_5_p2, binary_to_bcd_converter_5_p3,
       binary_to_bcd_converter_6_p1, binary_to_bcd_converter_6_p3, binary_to_bcd_converter_6_p4,
       binary_to_bcd_converter_7_p2, binary_to_bcd_converter_7_p3, binary_to_bcd_converter_8_p1,
       binary_to_bcd_converter_8_p3, binary_to_bcd_converter_8_p4, binary_to_bcd_converter_8_p5;
  wire [7:0] adder_1_out, execution_1_aluout_ex, execution_1_new_pc_ex, execution_1_regdata2_ex,
       instruction_decoding_1_new_pc_id, instruction_fetching_1_new_pc, instruction_fetching_1_opcode_if,
       memory_access_1_aluout_me, memory_access_1_new_pc_me, memory_access_1_readdatam_me, PC_q,
       register_file_1_regdata1_ex, register_file_1_regdata2_ex, register_file_1_regdata3_ex,
       write_back_1_new_pc_wb, write_back_1_writedatam_wb;

  Adder adder_1 (.a(8'h1), .b(write_back_1_new_pc_wb), .out(adder_1_out));  // open: cin, cout
  Clock #(.phaseOffset(1)) PC_Clock (.out(PC_Clock_out));
  Register PC (.D(adder_1_out), .en(1'b1), .clk(PC_Clock_out), .Q(PC_q));  // open: clr
  Instruction_Fetching instruction_fetching_1 (
    .PC(PC_q), .PC_Clock(PC_Clock_out), .New_PC(instruction_fetching_1_new_pc),
    .Opcode_IF(instruction_fetching_1_opcode_if));
  Instruction_Decoding instruction_decoding_1 (
    .New_PC_IF(instruction_fetching_1_new_pc), .Opcode_IF(instruction_fetching_1_opcode_if),
    .New_PC_ID(instruction_decoding_1_new_pc_id), .Rs_ID(instruction_decoding_1_rs_id),
    .Rt_ID(instruction_decoding_1_rt_id), .Rd_ID(instruction_decoding_1_rd_id),
    .WriteEnable_ID(instruction_decoding_1_writeenable_id), .ALUOp_ID(instruction_decoding_1_aluop_id),
    .MemRead_ID(instruction_decoding_1_memread_id), .MemWrite_ID(instruction_decoding_1_memwrite_id),
    .MemToReg_ID(instruction_decoding_1_memtoreg_id));
  Execution execution_1 (
    .New_PC_ID(instruction_decoding_1_new_pc_id), .RegData1_RF(register_file_1_regdata1_ex),
    .RegData2_RF(register_file_1_regdata2_ex), .RegData3_RF(register_file_1_regdata3_ex),
    .WriteReg_ID(instruction_decoding_1_rd_id), .WriteEnable_ID(instruction_decoding_1_writeenable_id),
    .ALUOp_ID(instruction_decoding_1_aluop_id), .MemRead_ID(instruction_decoding_1_memread_id),
    .MemWrite_ID(instruction_decoding_1_memwrite_id), .MemToReg_ID(instruction_decoding_1_memtoreg_id),
    .New_PC_EX(execution_1_new_pc_ex), .ALUOut_EX(execution_1_aluout_ex),
    .RegData2_EX(execution_1_regdata2_ex), .WriteReg_EX(execution_1_writereg_ex),
    .WriteEnable_EX(execution_1_writeenable_ex), .MemRead_EX(execution_1_memread_ex),
    .MemWrite_EX(execution_1_memwrite_ex), .MemToReg_EX(execution_1_memtoreg_ex));
  Memory_Access memory_access_1 (
    .PC_Clock(PC_Clock_out), .New_PC_EX(execution_1_new_pc_ex), .ALUOut_EX(execution_1_aluout_ex),
    .RegData2_EX(execution_1_regdata2_ex), .WriteReg_EX(execution_1_writereg_ex),
    .WriteEnable_EX(execution_1_writeenable_ex), .MemRead_EX(execution_1_memread_ex),
    .MemWrite_EX(execution_1_memwrite_ex), .MemToReg_EX(execution_1_memtoreg_ex),
    .New_PC_ME(memory_access_1_new_pc_me), .ALUOut_ME(memory_access_1_aluout_me),
    .WriteReg_ME(memory_access_1_writereg_me), .WriteEnable_ME(memory_access_1_writeenable_me),
    .MemToReg_ME(memory_access_1_memtoreg_me), .ReadDataM_ME(memory_access_1_readdatam_me));
  Write_Back write_back_1 (
    .New_PC_ME(memory_access_1_new_pc_me), .ALUOut_ME(memory_access_1_aluout_me),
    .WriteReg_ME(memory_access_1_writereg_me), .WriteEnable_ME(memory_access_1_writeenable_me),
    .MemToReg_ME(memory_access_1_memtoreg_me), .ReadDataM_ME(memory_access_1_readdatam_me),
    .New_PC_WB(write_back_1_new_pc_wb), .WriteDataM_WB(write_back_1_writedatam_wb));
  Register_File register_file_1 (
    .PC_Clock(PC_Clock_out), .WriteReg_ID(instruction_decoding_1_rd_id),
    .WriteEnable_ID(instruction_decoding_1_writeenable_id), .RegDataW(write_back_1_writedatam_wb),
    .ReadReg1_ID(instruction_decoding_1_rs_id), .ReadReg2_ID(instruction_decoding_1_rt_id),
    .RegData1_EX(register_file_1_regdata1_ex), .RegData2_EX(register_file_1_regdata2_ex),
    .RegData3_EX(register_file_1_regdata3_ex));
  Hex_Digit_Display hex_digit_display_1 (.value(binary_to_bcd_converter_1_p2));  // open: dp
  // Binary_to_BCD_converter #(.binvalue(8)) binary_to_bcd_converter_1: pin names not known; wires that end beside it: register_file_1_regdata1_ex, binary_to_bcd_converter_1_p2, binary_to_bcd_converter_1_p3
  Hex_Digit_Display hex_digit_display_2 (.value(binary_to_bcd_converter_2_p2));  // open: dp
  // Binary_to_BCD_converter #(.binvalue(8)) binary_to_bcd_converter_2: pin names not known; wires that end beside it: write_back_1_writedatam_wb, binary_to_bcd_converter_2_p2, binary_to_bcd_converter_2_p3, binary_to_bcd_converter_2_p4
  Hex_Digit_Display hex_digit_display_3 (.value(binary_to_bcd_converter_3_p2));  // open: dp
  // Binary_to_BCD_converter #(.binvalue(8)) binary_to_bcd_converter_3: pin names not known; wires that end beside it: PC_q, binary_to_bcd_converter_3_p2, binary_to_bcd_converter_3_p3, binary_to_bcd_converter_3_p4
  Hex_Digit_Display hex_digit_display_4 (.value(binary_to_bcd_converter_4_p2));  // open: dp
  Hex_Digit_Display hex_digit_display_5 (.value(binary_to_bcd_converter_4_p3));  // open: dp
  // Binary_to_BCD_converter #(.binvalue(4)) binary_to_bcd_converter_4: pin names not known; wires that end beside it: {2'b00, instruction_decoding_1_rd_id}, binary_to_bcd_converter_4_p2, binary_to_bcd_converter_4_p3
  Hex_Digit_Display hex_digit_display_6 (.value(binary_to_bcd_converter_1_p3));  // open: dp
  Hex_Digit_Display hex_digit_display_7 (.value(binary_to_bcd_converter_6_p1));  // open: dp
  Hex_Digit_Display hex_digit_display_8 (.value(binary_to_bcd_converter_2_p3));  // open: dp
  Hex_Digit_Display hex_digit_display_9 (.value(binary_to_bcd_converter_2_p4));  // open: dp
  Hex_Digit_Display hex_digit_display_10 (.value(binary_to_bcd_converter_3_p3));  // open: dp
  Hex_Digit_Display hex_digit_display_11 (.value(binary_to_bcd_converter_3_p4));  // open: dp
  Hex_Digit_Display hex_digit_display_12 (.value(binary_to_bcd_converter_5_p2));  // open: dp
  Hex_Digit_Display hex_digit_display_13 (.value(binary_to_bcd_converter_5_p3));  // open: dp
  // Binary_to_BCD_converter #(.binvalue(4)) binary_to_bcd_converter_5: pin names not known; wires that end beside it: {2'b00, instruction_decoding_1_rs_id}, binary_to_bcd_converter_5_p2, binary_to_bcd_converter_5_p3
  Hex_Digit_Display hex_digit_display_14 (.value(binary_to_bcd_converter_6_p3));  // open: dp
  // Binary_to_BCD_converter #(.binvalue(8)) binary_to_bcd_converter_6: pin names not known; wires that end beside it: binary_to_bcd_converter_6_p1, register_file_1_regdata2_ex, binary_to_bcd_converter_6_p3, binary_to_bcd_converter_6_p4
  Hex_Digit_Display hex_digit_display_15 (.value(binary_to_bcd_converter_6_p4));  // open: dp
  Hex_Digit_Display hex_digit_display_16 (.value(binary_to_bcd_converter_8_p1));  // open: dp
  Hex_Digit_Display hex_digit_display_17 (.value(binary_to_bcd_converter_7_p2));  // open: dp
  Hex_Digit_Display hex_digit_display_18 (.value(binary_to_bcd_converter_7_p3));  // open: dp
  // Binary_to_BCD_converter #(.binvalue(4)) binary_to_bcd_converter_7: pin names not known; wires that end beside it: {2'b00, instruction_decoding_1_rt_id}, binary_to_bcd_converter_7_p2, binary_to_bcd_converter_7_p3
  Hex_Digit_Display hex_digit_display_19 (.value(binary_to_bcd_converter_8_p3));  // open: dp
  // Binary_to_BCD_converter #(.binvalue(8)) binary_to_bcd_converter_8: pin names not known; wires that end beside it: binary_to_bcd_converter_8_p1, register_file_1_regdata3_ex, binary_to_bcd_converter_8_p3, binary_to_bcd_converter_8_p4, binary_to_bcd_converter_8_p5
  Hex_Digit_Display hex_digit_display_20 (.value(binary_to_bcd_converter_8_p4));  // open: dp
  Hex_Digit_Display hex_digit_display_21 (.value(binary_to_bcd_converter_8_p5));  // open: dp

  // Notes on the sheet:
  //   SleepyU
  //   Names: Yash Parmar & Nikunj Patel
  //   Pledge: I pledge my honor that I have abided by the Stevens Honor System.
  //   Rd
  //   RegData1
  //   ALUOut
  //   PC
  //   Rs
  //   RegData2
  //   Rt
  //   RegData3
endmodule

module Instruction_Fetching (
  input  [7:0] PC,
  input  PC_Clock,
  output [7:0] New_PC,
  output [7:0] Opcode_IF
);

  RAM #(.trigger("falling")) Instruction_RAM (
    .addr(PC), .we(1'b0), .oe(1'b1), .clk(PC_Clock), .dout(Opcode_IF));  // open: din

  assign New_PC = PC;

  // Notes on the sheet:
  //   Instruction Fetching Stage
endmodule

module Instruction_Decoding (
  input  [7:0] New_PC_IF,
  input  [7:0] Opcode_IF,
  output [7:0] New_PC_ID,
  output [1:0] Rs_ID,
  output [1:0] Rt_ID,
  output [1:0] Rd_ID,
  output WriteEnable_ID,
  output ALUOp_ID,
  output MemRead_ID,
  output MemWrite_ID,
  output MemToReg_ID
);

  wire decoder_1_out0;

  Decoder #(.enable("false"), .select(2)) decoder_1 (
    .out0(decoder_1_out0), .out1(ALUOp_ID), .out2(MemRead_ID), .out3(MemWrite_ID), .sel(Opcode_IF[7:6]));
  or or_1 (WriteEnable_ID, decoder_1_out0, ALUOp_ID, MemRead_ID);

  assign MemToReg_ID = MemRead_ID;
  assign New_PC_ID = New_PC_IF;
  assign Rd_ID = Opcode_IF[5:4];
  assign Rs_ID = Opcode_IF[3:2];
  assign Rt_ID = Opcode_IF[1:0];

  // Notes on the sheet:
  //   Rm/Rs
  //   Rn/Rt
  //   Rd
  //   Opcode
  //   Boost
  //   Fall
  //   Fetch
  //   Tuck
  //   Instruction Decoding Stage
  //   Source Register (2-bit)
  //   Target Register (2-bit)
  //   Destination Register (2-bit)
  //   MemRead (1-bit)
  //   MemToReg (1-bit)
  //   WriteEnable (1-bit)
  //   ALUOp (1-bit)
  //   MemWrite (1-bit)
endmodule

module Execution (
  input  [7:0] New_PC_ID,
  input  [7:0] RegData1_RF,
  input  [7:0] RegData2_RF,
  input  [7:0] RegData3_RF,
  input  [1:0] WriteReg_ID,
  input  WriteEnable_ID,
  input  ALUOp_ID,
  input  MemRead_ID,
  input  MemWrite_ID,
  input  MemToReg_ID,
  output [7:0] New_PC_EX,
  output [7:0] ALUOut_EX,
  output [7:0] RegData2_EX,
  output [1:0] WriteReg_EX,
  output WriteEnable_EX,
  output MemRead_EX,
  output MemWrite_EX,
  output MemToReg_EX
);

  wire [7:0] adder_1_out, subtractor_1_out;

  Subtractor subtractor_1 (.a(RegData1_RF), .b(RegData2_RF), .out(subtractor_1_out));  // open: bin, bout
  Adder adder_1 (.a(RegData1_RF), .b(RegData2_RF), .out(adder_1_out));  // open: cin, cout
  Multiplexer #(.width(8)) multiplexer_1 (.in0(adder_1_out), .in1(subtractor_1_out), .out(ALUOut_EX), .sel(ALUOp_ID));

  assign MemRead_EX = MemRead_ID;
  assign MemToReg_EX = MemToReg_ID;
  assign MemWrite_EX = MemWrite_ID;
  assign New_PC_EX = New_PC_ID;
  assign RegData2_EX = RegData3_RF;
  assign WriteEnable_EX = WriteEnable_ID;
  assign WriteReg_EX = WriteReg_ID;

  // Notes on the sheet:
  //   Execution Stage
endmodule

module Memory_Access (
  input  PC_Clock,
  input  [7:0] New_PC_EX,
  input  [7:0] ALUOut_EX,
  input  [7:0] RegData2_EX,
  input  [1:0] WriteReg_EX,
  input  WriteEnable_EX,
  input  MemRead_EX,
  input  MemWrite_EX,
  input  MemToReg_EX,
  output [7:0] New_PC_ME,
  output [7:0] ALUOut_ME,
  output [1:0] WriteReg_ME,
  output WriteEnable_ME,
  output MemToReg_ME,
  output [7:0] ReadDataM_ME
);

  RAM Data_RAM (
    .addr(ALUOut_EX), .we(MemWrite_EX), .oe(MemRead_EX), .clk(PC_Clock), .din(RegData2_EX),
    .dout(ReadDataM_ME));

  assign ALUOut_ME = ALUOut_EX;
  assign MemToReg_ME = MemToReg_EX;
  assign New_PC_ME = New_PC_EX;
  assign WriteEnable_ME = WriteEnable_EX;
  assign WriteReg_ME = WriteReg_EX;

  // Notes on the sheet:
  //   Memory Access Stage
endmodule

module Write_Back (
  input  [7:0] New_PC_ME,
  input  [7:0] ALUOut_ME,
  input  [1:0] WriteReg_ME,
  input  WriteEnable_ME,
  input  MemToReg_ME,
  input  [7:0] ReadDataM_ME,
  output [7:0] New_PC_WB,
  output [7:0] WriteDataM_WB
);

  Multiplexer #(.width(8)) multiplexer_1 (.in0(ALUOut_ME), .in1(ReadDataM_ME), .out(WriteDataM_WB), .sel(MemToReg_ME));

  assign New_PC_WB = New_PC_ME;

  // Notes on the sheet:
  //   Write Back Stage
endmodule

module Register_File (
  input  PC_Clock,
  input  [1:0] WriteReg_ID,
  input  WriteEnable_ID,
  input  [7:0] RegDataW,
  input  [1:0] ReadReg1_ID,
  input  [1:0] ReadReg2_ID,
  output [7:0] RegData1_EX,
  output [7:0] RegData2_EX,
  output [7:0] RegData3_EX
);

  wire and_1_out, and_2_out, and_3_out, and_4_out, decoder_1_out0, decoder_1_out1, decoder_1_out2,
       decoder_1_out3;
  wire [7:0] X0_q, X1_q, X2_q, X3_q;

  Decoder #(.enable("false"), .select(2)) decoder_1 (
    .out0(decoder_1_out0), .out1(decoder_1_out1), .out2(decoder_1_out2), .out3(decoder_1_out3),
    .sel(WriteReg_ID));
  Register #(.trigger("falling")) X0 (.D(RegDataW), .en(and_1_out), .clk(PC_Clock), .Q(X0_q));  // open: clr
  and and_1 (and_1_out, WriteEnable_ID, decoder_1_out0);
  Register #(.trigger("falling")) X1 (.D(RegDataW), .en(and_2_out), .clk(PC_Clock), .Q(X1_q));  // open: clr
  and and_2 (and_2_out, WriteEnable_ID, decoder_1_out1);
  Register #(.trigger("falling")) X2 (.D(RegDataW), .en(and_3_out), .clk(PC_Clock), .Q(X2_q));  // open: clr
  and and_3 (and_3_out, WriteEnable_ID, decoder_1_out2);
  Register #(.trigger("falling")) X3 (.D(RegDataW), .en(and_4_out), .clk(PC_Clock), .Q(X3_q));  // open: clr
  and and_4 (and_4_out, WriteEnable_ID, decoder_1_out3);
  Multiplexer #(.select(2), .width(8)) multiplexer_1 (
    .in0(X0_q), .in1(X1_q), .in2(X2_q), .in3(X3_q), .out(RegData1_EX), .sel(ReadReg1_ID));
  Multiplexer #(.select(2), .width(8)) multiplexer_2 (
    .in0(X0_q), .in1(X1_q), .in2(X2_q), .in3(X3_q), .out(RegData2_EX), .sel(ReadReg2_ID));
  Multiplexer #(.select(2), .width(8)) multiplexer_3 (
    .in0(X0_q), .in1(X1_q), .in2(X2_q), .in3(X3_q), .out(RegData3_EX), .sel(WriteReg_ID));

  // Notes on the sheet:
  //   Register File
endmodule
